// Digital circuit 4bit_adder_complete.dig as structural Verilog
module _4bit_adder_complete (
  input  A0,
  input  B0,
  input  Cin,
  input  A1,
  input  B1,
  input  A2,
  input  B2,
  input  A3,
  input  B3,
  output S0,
  output S1,
  output S2,
  output S3,
  output Cout
);

  wire and_1_out, and_2_out, and_3_out, and_4_out, and_5_out, and_6_out, and_7_out, and_8_out, and_9_out,
       and_10_out, and_11_out, and_12_out, and_13_out, and_14_out, and_15_out, and_16_out, and_17_out,
       and_18_out, and_19_out, and_20_out, and_21_out, and_22_out, and_23_out, and_24_out, and_25_out,
       and_26_out, and_27_out, and_28_out, and_29_out, and_30_out, and_31_out, and_32_out, or_3_out,
       or_4_out, or_7_out;

  and and_1 (and_1_out, A1, B1, or_4_out);
  and and_2 (and_2_out, ~A1, ~B1, or_4_out);  // And
  and and_3 (and_3_out, ~A1, B1, ~or_4_out);  // And
  and and_4 (and_4_out, A1, ~B1, ~or_4_out);  // And
  and and_5 (and_5_out, ~A1, B1, or_4_out);  // And
  and and_6 (and_6_out, A1, ~B1, or_4_out);  // And
  and and_7 (and_7_out, A1, B1, ~or_4_out);  // And
  and and_8 (and_8_out, A1, B1, or_4_out);
  and and_9 (and_9_out, A0, B0, Cin);
  and and_10 (and_10_out, ~A0, ~B0, Cin);  // And
  and and_11 (and_11_out, ~A0, B0, ~Cin);  // And
  or or_1 (S1, and_1_out, and_2_out, and_3_out, and_4_out);
  and and_12 (and_12_out, A0, ~B0, ~Cin);  // And
  and and_13 (and_13_out, ~A0, B0, Cin);  // And
  and and_14 (and_14_out, A0, ~B0, Cin);  // And
  and and_15 (and_15_out, A0, B0, ~Cin);  // And
  and and_16 (and_16_out, A0, B0, Cin);
  or or_2 (S0, and_9_out, and_10_out, and_11_out, and_12_out);
  or or_3 (or_3_out, and_5_out, and_6_out, and_7_out, and_8_out);
  or or_4 (or_4_out, and_13_out, and_14_out, and_15_out, and_16_out);
  and and_17 (and_17_out, A2, B2, or_3_out);
  and and_18 (and_18_out, ~A2, ~B2, or_3_out);  // And
  and and_19 (and_19_out, ~A2, B2, ~or_3_out);  // And
  and and_20 (and_20_out, A2, ~B2, ~or_3_out);  // And
  and and_21 (and_21_out, ~A2, B2, or_3_out);  // And
  and and_22 (and_22_out, A2, ~B2, or_3_out);  // And
  and and_23 (and_23_out, A2, B2, ~or_3_out);  // And
  and and_24 (and_24_out, A2, B2, or_3_out);
  and and_25 (and_25_out, A3, B3, or_7_out);
  and and_26 (and_26_out, ~A3, ~B3, or_7_out);  // And
  and and_27 (and_27_out, ~A3, B3, ~or_7_out);  // And
  and and_28 (and_28_out, A3, ~B3, ~or_7_out);  // And
  and and_29 (and_29_out, ~A3, B3, or_7_out);  // And
  and and_30 (and_30_out, A3, ~B3, or_7_out);  // And
  and and_31 (and_31_out, A3, B3, ~or_7_out);  // And
  and and_32 (and_32_out, A3, B3, or_7_out);
  or or_5 (S2, and_17_out, and_18_out, and_19_out, and_20_out);
  or or_6 (S3, and_25_out, and_26_out, and_27_out, and_28_out);
  or or_7 (or_7_out, and_21_out, and_22_out, and_23_out, and_24_out);
  or or_8 (Cout, and_29_out, and_30_out, and_31_out, and_32_out);
endmodule
