// Digital circuit full_adder_complete.dig as structural Verilog
module full_adder_complete (
  input  A,
  input  B,
  input  C,
  output Sum,
  output Cout
);

  wire and_1_out, and_2_out, and_3_out, and_4_out, and_5_out, and_6_out, and_7_out, and_8_out;

  and and_1 (and_1_out, A, B, C);
  and and_2 (and_2_out, ~A, ~B, C);  // And
  and and_3 (and_3_out, ~A, B, ~C);  // And
  and and_4 (and_4_out, A, ~B, ~C);  // And
  and and_5 (and_5_out, ~A, B, C);  // And
  and and_6 (and_6_out, A, ~B, C);  // And
  and and_7 (and_7_out, A, B, ~C);  // And
  and and_8 (and_8_out, A, B, C);
  or or_1 (Sum, and_1_out, and_2_out, and_3_out, and_4_out);
  or or_2 (Cout, and_5_out, and_6_out, and_7_out, and_8_out);
endmodule
